# Fritzing sketch v.1.0 (saved by Fritzing 0.9.0b)
breadboards: 1

parts:
  Bauteil1 = Arduino Uno (Rev3)
  RF1 = nRF8001 Bluetooth LE Breakout
  TFT1 = 2.2" TFT with MicroSD Breakout

nets:
  N1: Bauteil1.D9_PWM, TFT1.SDCS
  N2: Bauteil1.D10_PWM/SS, TFT1.CS
  N3: Bauteil1.D11_PWM/MOSI, RF1.MOSI, TFT1.MOSI
  N4: Bauteil1.D12/MISO, RF1.MISO, TFT1.MISO
  N5: Bauteil1.D13/SCK, RF1.SCK, TFT1.SCK
  N6: Bauteil1.D2, RF1.RDY
  N7: Bauteil1.D3_PWM, TFT1.BL
  N8: Bauteil1.D6_PWM, RF1.REQ
  N9: Bauteil1.D7, RF1.RST
  5V: Bauteil1.5V, TFT1.RST, TFT1.VIN
  GND: Bauteil1.GND, RF1.GND, TFT1.GND
  VIN: Bauteil1.VIN, RF1.VIN

custom parts:
  nRF8001 Bluetooth LE Breakout: nRF8001 Breakout Board
  2.2" TFT with MicroSD Breakout: 2.2" TFT Display with HX8340B Controller and MicroSD Card
